# Fritzing sketch TheCatUnFeeder (saved by Fritzing 0.9.3b)
breadboards: 1

parts:
  Part1 = Arduino Nano (Rev3.0)
  Q1 = NPN-Transistor [package="TO92 [THT]"]
  LED1 = LED - 5mm [color="White (6500K)" package="5 mm [THT]"]
  LED2 = LED - 5mm [color="White (6500K)" package="5 mm [THT]"]
  R2 = Resistor [tolerance=±1% resistance=100 package=THT]
  R3 = Resistor [tolerance=±1% resistance=100 package=THT]
  J1 = Basic Servo
  R1 = Resistor [tolerance=±1% resistance=3.3k package=THT]
  Part2 = RFID-RC522-v2
  C1 = Electrolytic Capacitor [capacitance=470µF package="100 mil [THT, electrolytic]"]

nets:
  GND: Part1.GND, Q1.E, J1.gnd, Part2.GND, C1.-
  N1: Part1.D6, R1.Pin_1
  N2: Part1.D8, J1.pulse
  N3: Part1.D11/MOSI, Part2.MOSI
  N4: Part1.D12/MISO, Part2.MISO
  VIN: Part1.VIN, R2.Pin_0, J1.vcc, C1.+
  N5: Part1.A4, Part2.SDA
  3V3: Part1.3V3, Part2.3.3V
  N6: Part1.D13/SCK, Part2.SCK
  N7: Q1.B, R1.Pin_0
  N8: Q1.C, LED1.cathode, LED2.cathode
  N9: LED1.anode, R3.Pin_1
  N10: LED2.anode, R2.Pin_1

notes:
  5v
  3.3V

custom parts:
  RFID-RC522-v2: A simple China made RFID-RC522 Reader; do check the pin labels, as this is a MFRC522 based clone.
